# Fritzing sketch esp32_ads1115_getting_started (saved by Fritzing 0.9.3b)
breadboards: 1

parts:
  U1 = ESP32S-HiLetgo [part_number=ESP32S-HiLetgo]
  Part1 = Adafruit ADS1115 16Bit I2C ADC [part_number="Adafruit #1085"]
  U2 = POT [package=alps_pot]

nets:
  N1: U1.3.3, Part1.VDD, U2.E
  GND: U1.GND, Part1.ADDR, Part1.GND, U2.A
  N2: U1.GPIO21, Part1.SDA
  N3: U1.GPIO22, Part1.SCL
  N4: Part1.AIN0, U2.S

notes:
  The ESP32 that I am using for this diagram is based on the ESP32E model. Always be sure to double-check the I2C pins if you are using a different model.

custom parts:
  ESP32S-HiLetgo: HiLetgo ESP-WROOM-32 ESP32 ESP-32S Development Board 2.4GHz Dual-Mode WiFi + Bluetooth Dual Cores Microcontroller The ESP32 integrated with Antenna switches, RF Balun, power amplifiers, low-noise amplifiers, filters, and management modules, and the entire solution occupies the least area of PCB. 2.4 GHz Wi-Fi plus Bluetooth dual-mode chip, with TSMC Ultra-low power consumption 40nm technology,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
  Adafruit ADS1115 16Bit I2C ADC: For microcontrollers without an analog-to-digital converter or when you want a higher-precision ADC, the ADS1115 provides 16-bit precision at 860 samples/second over I2C. The chip can be configured as 4 single-ended input channels, or two differential channels. As a nice bonus, it even includes a programmable gain amplifier, up to x16, to help boost up smaller single/differential signals to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
